# Fritzing sketch Strobe_wired (saved by Fritzing 0.9.3b)
breadboards: 1

parts:
  R1 = Resistor [tolerance=±5% resistance=220 package=THT]
  S1 = Pushbutton [package="[THT]"]
  Part1 = Arduino Uno (Rev3)
  R2 = Resistor [tolerance=±5% resistance=220 package=THT]
  LED1 = LED - 5mm [color="Red (660nm)" package="5 mm [THT]"]

nets:
  N1: R1.Pin_0, Part1.GND, R2.Pin_0
  N2: R1.Pin_1, S1.Pin_1, S1.Pin_2, Part1.D2
  N3: S1.Pin_3, S1.Pin_4, Part1.5V
  N4: Part1.D11_PWM/MOSI, LED1.anode
  N5: R2.Pin_1, LED1.cathode
